# Fritzing sketch DevreŞeması (saved by Fritzing 0.9.3b)
breadboards: 1

parts:
  Parça1 = Arduino Uno (Rev3)
  J1 = Piezo Speaker
  J3 = Basic Servo
  LED1 = RGB LED (com. cathode, rbg) [package="5 mm [THT]"]
  Parça2 = Bluetooth HC-05 Macho
  J4 = Basic Servo

nets:
  N1: Parça1.D9_PWM, J3.pulse
  N2: Parça1.D10_PWM/SS, J4.pulse
  N3: Parça1.D0/RX, Parça2.TXD
  N4: Parça1.D1/TX, Parça2.RXD
  N5: Parça1.D2, J1.pin2
  GND: J1.pin1, J3.gnd, LED1.blue_anode, Parça2.GND, J4.gnd
  VCC: J3.vcc, Parça2.VCC, J4.vcc
